# Fritzing sketch receiver (saved by Fritzing 0.9.2b)
breadboards: 1

parts:
  RJ45 = RJ45 Jack [package=rj45-8]
  MAX485 = MAX485 [package=dil08]
  R1 = Resistor [tolerance=±5% resistance=120 package=THT]
  VCC1 = Battery
  U1 = Voltage Regulator - 5V [package="TO220 [THT]"]  # not connected
  R2 = Resistor [tolerance=±5% resistance=470k package=THT]
  R3 = Resistor [tolerance=±5% resistance=470k package=THT]

nets:
  N1: RJ45.1, MAX485.A, R1.Pin_0, R3.Pin_1
  N2: RJ45.2, MAX485.B, R1.Pin_1, R2.Pin_1
  N3: MAX485.RE, MAX485.DE
  N4: MAX485.GND, VCC1.-, R3.Pin_0
  N5: MAX485.VCC, VCC1.+, R2.Pin_0
